# Fritzing sketch iot-raspi-blinky (saved by Fritzing 0.9.9b)
breadboards: 1

parts:
  Mod1 = Raspberry Pi 4B
  LED1 = LED - 5mm [color="Red (633nm)" current=0.030 package="5 mm [THT]"]
  R1 = Resistor [tolerance=±5% power=0.25 resistance=68 package=THT]

nets:
  N1: Mod1.GND, R1.Pin_1
  N2: Mod1.GPIO18, LED1.anode
  N3: LED1.cathode, R1.Pin_0
